// Logisim project CSE-231.07 LAB PROJECT FINAL WORK COMBINATIONAL AND SEQUENTIAL CIRCUIT BOTH PARTS.circ as structural Verilog
module main (
  input  in_1
);

  wire and_1_out, and_2_out, and_3_out, and_4_out, and_5_out, and_6_out, and_7_out, and_8_out, and_9_out,
       and_10_out, clock_1_out, j_k_ff_1_q, j_k_ff_2_q, j_k_ff_3_q, not_1_out, not_2_out, not_3_out,
       or_1_out, or_2_out, or_3_out, or_4_out, or_5_out, or_6_out, xnor_1_out, xnor_2_out, xor_1_out;

  Clock clock_1 (.out(clock_1_out));
  J_K_Flip_Flop j_k_ff_1 (.J(1'b1), .clk(j_k_ff_2_q), .K(1'b1), .Q(j_k_ff_1_q));  // open: Qn, preset, en, reset
  J_K_Flip_Flop j_k_ff_2 (.J(1'b1), .clk(j_k_ff_3_q), .K(1'b1), .Q(j_k_ff_2_q));  // open: Qn, preset, en, reset
  J_K_Flip_Flop j_k_ff_3 (.J(1'b1), .clk(clock_1_out), .K(1'b1), .Q(j_k_ff_3_q));  // open: Qn, preset, en, reset
  not not_1 (not_1_out, j_k_ff_1_q);
  not not_2 (not_2_out, j_k_ff_2_q);
  not not_3 (not_3_out, j_k_ff_3_q);
  and and_1 (and_1_out, j_k_ff_1_q, not_3_out);
  and and_2 (and_2_out, not_1_out, j_k_ff_2_q);
  and and_3 (and_3_out, not_2_out, j_k_ff_3_q);
  and and_4 (and_4_out, not_1_out, j_k_ff_3_q);
  and and_5 (and_5_out, not_2_out, j_k_ff_3_q);
  and and_6 (and_6_out, j_k_ff_1_q, j_k_ff_2_q, not_3_out);
  and and_7 (and_7_out, not_1_out, not_2_out, j_k_ff_3_q);
  and and_8 (and_8_out, not_2_out, j_k_ff_3_q);
  and and_9 (and_9_out, not_1_out, j_k_ff_3_q);
  and and_10 (and_10_out, not_1_out, j_k_ff_3_q);
  xor xor_1 (xor_1_out, not_2_out, not_3_out);
  xnor xnor_1 (xnor_1_out, not_1_out, not_2_out);
  xnor xnor_2 (xnor_2_out, not_1_out, not_3_out);
  or or_1 (or_1_out, and_8_out, and_9_out);
  or or_2 (or_2_out, and_10_out, xor_1_out);
  or or_3 (or_3_out, xnor_1_out, not_3_out);
  or or_4 (or_4_out, and_1_out, and_2_out, and_3_out);
  or or_5 (or_5_out, xnor_2_out, j_k_ff_2_q);
  or or_6 (or_6_out, and_4_out, and_5_out, and_6_out);
  _7_Segment_Display u_7_segment_display_1 (
    .g(or_5_out), .f(or_4_out), .a(or_6_out), .b(and_7_out), .e(or_3_out), .d(or_2_out), .c(or_1_out),
    .dp(in_1));

  // Notes on the sheet:
  //   A
  //   B
  //   C
  //   a
  //        b
  //   d
  //   e
  //   f
  //   g
  //   c
  //   Group-6
  //   000-r
  //   001-E
  //   010-S
  //   011-I
  //   100-S
  //   101-t
  //   110-O
  //   111-r
endmodule
