// Logisim project project simulation 2.circ as structural Verilog
module main (
  input  A,
  input  B,
  input  C,
  input  in_4
);

  wire and_1_out, and_2_out, and_3_out, and_4_out, and_5_out, and_6_out, and_7_out, and_8_out, and_9_out,
       and_10_out, not_1_out, not_2_out, not_3_out, or_1_out, or_2_out, or_3_out, or_4_out, or_5_out,
       or_6_out, xnor_1_out, xnor_2_out, xor_1_out;

  not not_1 (not_1_out, A);
  not not_2 (not_2_out, B);
  not not_3 (not_3_out, C);
  and and_1 (and_1_out, A, not_3_out);
  and and_2 (and_2_out, B, not_3_out);
  and and_3 (and_3_out, not_1_out, not_2_out, C);
  and and_4 (and_4_out, A, B, not_3_out);
  and and_5 (and_5_out, B, not_3_out);
  and and_6 (and_6_out, A, not_3_out);
  and and_7 (and_7_out, A, not_3_out);
  xor xor_1 (xor_1_out, B, C);
  xnor xnor_1 (xnor_1_out, A, B);
  and and_8 (and_8_out, not_1_out, C);
  and and_9 (and_9_out, A, not_2_out);
  and and_10 (and_10_out, B, not_3_out);
  xnor xnor_2 (xnor_2_out, A, C);
  or or_1 (or_1_out, xnor_1_out, C);
  or or_2 (or_2_out, and_8_out, and_9_out, and_10_out);
  or or_3 (or_3_out, xnor_2_out, not_2_out);
  or or_4 (or_4_out, and_1_out, and_2_out, and_3_out);
  or or_5 (or_5_out, and_5_out, and_6_out);
  or or_6 (or_6_out, and_7_out, xor_1_out);
  _7_Segment_Display u_7_segment_display_1 (
    .g(or_3_out), .f(or_2_out), .a(or_4_out), .b(and_4_out), .e(or_1_out), .d(or_6_out), .c(or_5_out),
    .dp(in_4));

  // Notes on the sheet:
  //   a
  //        b
  //   c
  //   d
  //   e
  //   f
  //   g
  //   Group-6
  //   000-r
  //   001-E
  //   010-S
  //   011-I
  //   100-S
  //   101-t
  //   110-O
  //   111-r
endmodule
